// Logisim project TO DO list.circ as structural Verilog: 1 circuit, main circuit main
module main (
  input  Print_Maps,
  input  Understand_Box_java,
  input  Save_Relationship,
  input  Save,
  input  LOAD_OPEN,
  input  Binding,
  input  Box_____ClassBox,
  input  Draw_Lines_Between_ClassBoxes,
  input  Center_of_Box,
  input  Event_Handler_Fixed,
  input  Draw_Arrow_Types,
  input  Collision_Points,
  input  Images_For_Those_Arrows,
  input  Draw_One_Arrow_Anywhere,
  input  Rotate_It,
  input  Repeat_For_Rest,
  input  DELETE,
  input  Side_Panel,
  input  Create_Button_Tied_to_Action
);

  wire and_1_out, and_2_out, and_3_out, and_4_out, and_5_out, and_6_out, and_7_out, and_8_out, and_9_out,
       and_10_out, and_11_out;

  LED Task_Completed (.in(and_1_out));
  LED Task_Completed_2 (.in(and_2_out));
  LED Task_Completed_3 (.in(and_4_out));
  and and_1 (and_1_out, and_5_out, LOAD_OPEN);
  and and_2 (and_2_out, and_3_out, Draw_Arrow_Types);
  LED led_1 (.in(and_3_out));
  and and_3 (and_3_out, Draw_Lines_Between_ClassBoxes, Binding, and_8_out, Images_For_Those_Arrows);
  and and_4 (and_4_out, Binding, and_6_out, DELETE);
  LED led_2 (.in(and_5_out));
  and and_5 (and_5_out, and_7_out, Save);
  LED led_3 (.in(and_6_out));
  and and_6 (and_6_out, Side_Panel, Create_Button_Tied_to_Action);
  LED led_4 (.in(and_7_out));
  and and_7 (and_7_out, and_9_out, Print_Maps, Save_Relationship, Box_____ClassBox);
  LED led_5 (.in(and_8_out));
  and and_8 (and_8_out, Center_of_Box, and_10_out, Collision_Points);
  LED led_6 (.in(and_9_out));
  and and_9 (and_9_out, Understand_Box_java, Binding);
  LED led_7 (.in(and_10_out));
  and and_10 (and_10_out, Event_Handler_Fixed, and_11_out);
  and and_11 (and_11_out, Repeat_For_Rest, Rotate_It, Draw_One_Arrow_Anywhere);
endmodule
